# Fritzing sketch hopeworks_codeday_fritzing_project (saved by Fritzing 0.9.3b)
circuit board: 5.68241cm x 3.8924cm
breadboards: 1

parts:
  Photon_Photoresistor_Project = Photon
  Photoresistor = PHOTOCELL [package=photocell]
  10kΩ = Resistor [tolerance=±5% resistance=10k package="0402 [SMD]"]
  LED = smd LED [color="Red (633nm)" package="0805 [SMD]"]
  330Ω = Resistor [tolerance=±5% resistance=330 package="0402 [SMD]"]

nets:
  N1: Photon_Photoresistor_Project.A0, Photoresistor.P$2, 10kΩ.Pin_0
  N2: Photon_Photoresistor_Project.GND, 10kΩ.Pin_1, 330Ω.Pin_1
  N3: Photon_Photoresistor_Project.D2, LED.anode
  N4: Photon_Photoresistor_Project.3V3, Photoresistor.P$1
  N5: LED.cathode, 330Ω.Pin_0

notes:
  -
